// Logisim project a1-2-Little.circ as structural Verilog: 1 circuit, main circuit main
module main (
  input  Y,
  input  Z,
  input  X,
  output F
);

  wire nand_1_out, nand_2_out, not_1_out;

  not not_1 (not_1_out, X);
  nand nand_1 (nand_1_out, Y, not_1_out);
  nand nand_2 (nand_2_out, X, Z);
  nand nand_3 (F, nand_1_out, nand_2_out);

  // Notes on the sheet:
  //   Mike Little
  //   1/19/13
  //   MUX with a=y, b=z, sel=z
endmodule
