// Logisim project a1-3-Little.circ as structural Verilog: 1 circuit, main circuit main
module main (
  input  A,
  input  B,
  output F
);

  wire nand_1_out, or_1_out;

  or or_1 (or_1_out, A, B);
  nand nand_1 (nand_1_out, A, B);
  and and_1 (F, or_1_out, nand_1_out);

  // Notes on the sheet:
  //   Mike Little
  //   1/19/13
  //   simple XOR gate
endmodule
