// Logisim project Assignment2.circ as structural Verilog: 2 circuits, main circuit main
module main (
);

  wire clock_1_out, n1_1_a_2, n1_1_b_2, n1_1_c_2, n1_1_d_2, n1_1_e, n1_1_f, n1_1_g;
  wire [3:0] counter_1_q;

  Counter #(.width(4), .max('hf)) counter_1 (.Q(counter_1_q), .clk(clock_1_out));  // open: load, D, count, carry, clr
  Clock clock_1 (.out(clock_1_out));
  LED N1 (.in(counter_1_q[1]));
  LED N2 (.in(counter_1_q[2]));
  LED N3 (.in(counter_1_q[3]));
  LED N0 (.in(counter_1_q[0]));
  _1 u_1_1 (
    .A(counter_1_q[3]), .B(counter_1_q[2]), .C(counter_1_q[1]), .D(counter_1_q[0]), .a_2(n1_1_a_2),
    .b_2(n1_1_b_2), .c_2(n1_1_c_2), .d_2(n1_1_d_2), .e(n1_1_e), .f(n1_1_f), .g(n1_1_g));
  _7_Segment_Display u_7_segment_display_1 (
    .g(n1_1_g), .f(n1_1_f), .a(n1_1_a_2), .b(n1_1_b_2), .e(n1_1_e), .d(n1_1_d_2), .c(n1_1_c_2));  // open: dp
endmodule

module _1 (
  input  A,
  input  B,
  input  C,
  input  D,
  output a_2,
  output b_2,
  output c_2,
  output d_2,
  output e,
  output f,
  output g
);

  wire and_1_out, and_2_out, and_3_out, and_4_out, and_5_out, and_6_out, and_7_out, and_8_out, and_9_out,
       and_10_out, and_11_out, and_12_out, and_13_out, and_14_out, and_15_out, and_16_out, and_17_out,
       and_18_out, and_19_out, and_20_out, and_21_out, and_22_out, and_23_out, and_24_out, and_25_out,
       and_26_out, and_27_out, and_28_out, and_29_out, and_30_out, and_31_out, and_32_out, and_33_out,
       and_34_out, and_35_out, and_36_out;

  and and_1 (and_1_out, ~A, C);  // AND_Gate
  and and_2 (and_2_out, B, C);
  and and_3 (and_3_out, A, ~D);  // AND_Gate
  and and_4 (and_4_out, ~B, ~D);  // AND_Gate
  and and_5 (and_5_out, ~A, B, D);  // AND_Gate
  and and_6 (and_6_out, A, ~B, ~C);  // AND_Gate
  and and_7 (and_7_out, ~B, ~C);  // AND_Gate
  and and_8 (and_8_out, ~B, ~D);  // AND_Gate
  and and_9 (and_9_out, ~A, ~C, ~D);  // AND_Gate
  and and_10 (and_10_out, ~A, C, D);  // AND_Gate
  and and_11 (and_11_out, A, ~C, D);  // AND_Gate
  and and_12 (and_12_out, ~A, B);  // AND_Gate
  and and_13 (and_13_out, A, ~B);  // AND_Gate
  and and_14 (and_14_out, ~C, D);  // AND_Gate
  and and_15 (and_15_out, ~A, ~C);  // AND_Gate
  and and_16 (and_16_out, ~A, D);  // AND_Gate
  and and_17 (and_17_out, B, ~C, D);  // AND_Gate
  and and_18 (and_18_out, ~B, C, D);  // AND_Gate
  and and_19 (and_19_out, B, C, ~D);  // AND_Gate
  and and_20 (and_20_out, A, ~C, ~D);  // AND_Gate
  and and_21 (and_21_out, ~A, ~B, ~D);  // AND_Gate
  and and_22 (and_22_out, A, B);
  and and_23 (and_23_out, C, ~D);  // AND_Gate
  and and_24 (and_24_out, A, C);
  and and_25 (and_25_out, A, ~D);  // AND_Gate
  and and_26 (and_26_out, ~B, ~D);  // AND_Gate
  and and_27 (and_27_out, A, ~B);  // AND_Gate
  and and_28 (and_28_out, ~C, ~D);  // AND_Gate
  and and_29 (and_29_out, B, ~D);  // AND_Gate
  and and_30 (and_30_out, A, C);
  and and_31 (and_31_out, ~A, B, ~C);  // AND_Gate
  and and_32 (and_32_out, A, ~B);  // AND_Gate
  and and_33 (and_33_out, C, ~D);  // AND_Gate
  and and_34 (and_34_out, A, D);
  and and_35 (and_35_out, ~B, C);  // AND_Gate
  and and_36 (and_36_out, ~A, B, ~C);  // AND_Gate
  or or_1 (a_2, and_1_out, and_2_out, and_3_out, and_4_out, and_5_out, and_6_out);
  or or_2 (b_2, and_7_out, and_8_out, and_9_out, and_10_out, and_11_out);
  or or_3 (c_2, and_12_out, and_13_out, and_14_out, and_15_out, and_16_out);
  or or_4 (d_2, and_17_out, and_18_out, and_19_out, and_20_out, and_21_out);
  or or_5 (e, and_22_out, and_23_out, and_24_out, and_25_out, and_26_out);
  or or_6 (f, and_27_out, and_28_out, and_29_out, and_30_out, and_31_out);
  or or_7 (g, and_32_out, and_33_out, and_34_out, and_35_out, and_36_out);
endmodule
