// Logisim project MARIE Project.circ as structural Verilog
module main (
);

  wire Clock_out, Control_Unit_r0, Control_Unit_r1, Control_Unit_r2, Control_Unit_w0, Control_Unit_w1,
       Control_Unit_w2, ir_1_w_bus;

  Control_Unit Control_Unit (
    .R0(Control_Unit_r0), .R1(Control_Unit_r1), .R2(Control_Unit_r2), .W0(Control_Unit_w0),
    .W1(Control_Unit_w1), .W2(Control_Unit_w2), .Clock(Clock_out));
  IR ir_1 (
    .R2(Control_Unit_r2), .R1(Control_Unit_r1), .R0(Control_Unit_r0), .R_Bus(ir_1_w_bus), .W_Bus(ir_1_w_bus),
    .W2(Control_Unit_w2), .W1(Control_Unit_w1), .W0(Control_Unit_w0), .Clock(Clock_out));
  Clock Clock (.out(Clock_out));
  OUT out_1 (
    .R2(Control_Unit_r2), .R1(Control_Unit_r1), .R0(Control_Unit_r0), .R_Bus(ir_1_w_bus), .W_Bus(ir_1_w_bus),
    .W2(Control_Unit_w2), .W1(Control_Unit_w1), .W0(Control_Unit_w0), .Clock(Clock_out));
  IN in_1 (
    .R2(Control_Unit_r2), .R1(Control_Unit_r1), .R0(Control_Unit_r0), .R_Bus(ir_1_w_bus), .W_Bus(ir_1_w_bus),
    .W2(Control_Unit_w2), .W1(Control_Unit_w1), .W0(Control_Unit_w0), .Clock(Clock_out));
  AC ac_1 (
    .R2(Control_Unit_r2), .R1(Control_Unit_r1), .R0(Control_Unit_r0), .R_Bus(ir_1_w_bus), .W_Bus(ir_1_w_bus),
    .W2(Control_Unit_w2), .W1(Control_Unit_w1), .W0(Control_Unit_w0), .Clock(Clock_out));
  MBR mbr_1 (
    .R2(Control_Unit_r2), .R1(Control_Unit_r1), .R0(Control_Unit_r0), .R_Bus(ir_1_w_bus), .W_Bus(ir_1_w_bus),
    .W2(Control_Unit_w2), .W1(Control_Unit_w1), .W0(Control_Unit_w0), .Clock(Clock_out));
  PC pc_1 (
    .R2(Control_Unit_r2), .R1(Control_Unit_r1), .R0(Control_Unit_r0), .R_Bus(ir_1_w_bus), .W_Bus(ir_1_w_bus),
    .W2(Control_Unit_w2), .W1(Control_Unit_w1), .W0(Control_Unit_w0), .Clock(Clock_out));
  MAR mar_1 (
    .R2(Control_Unit_r2), .R1(Control_Unit_r1), .R0(Control_Unit_r0), .R_Bus(ir_1_w_bus), .W_Bus(ir_1_w_bus),
    .W2(Control_Unit_w2), .W1(Control_Unit_w1), .W0(Control_Unit_w0), .Clock(Clock_out));
  Main_Memory Main_Memory (
    .R0(Control_Unit_r0), .R1(Control_Unit_r1), .R2(Control_Unit_r2), .W0(Control_Unit_w0),
    .W1(Control_Unit_w1), .W2(Control_Unit_w2), .R_Bus(ir_1_w_bus), .W_Bus(ir_1_w_bus), .Clock(Clock_out));
endmodule

module Control_Unit (
  input  Clock,
  output R0,
  output R1,
  output R2,
  output W0,
  output W1,
  output W2
);


  assign R0 = 1'b0;
  assign R1 = 1'b0;
  assign R2 = 1'b0;
  assign W0 = 1'b0;
  assign W1 = 1'b0;
  assign W2 = 1'b1;
endmodule

module IR (
  input  R2,
  input  R1,
  input  R0,
  input  R_Bus,
  input  W2,
  input  W1,
  input  W0,
  input  Clock,
  output W_Bus
);

  wire and_1_out, and_2_out, controlled_buffer_1_out, not_1_out, not_2_out, not_3_out, not_4_out, not_5_out,
       not_6_out, register_1_q;

  not not_1 (not_1_out, R2);
  and and_1 (and_1_out, not_1_out, not_2_out, not_3_out);
  not not_2 (not_2_out, R1);
  not not_3 (not_3_out, R0);
  assign controlled_buffer_1_out = and_1_out ? R_Bus : 1'bz;  // Controlled_Buffer controlled_buffer_1
  assign W_Bus = and_2_out ? register_1_q : 1'bz;  // Controlled_Buffer controlled_buffer_2
  and and_2 (and_2_out, not_4_out, not_5_out, not_6_out);
  Register #(.width(1)) register_1 (.D(controlled_buffer_1_out), .Q(register_1_q), .clk(Clock));  // open: en, clr
  not not_4 (not_4_out, W2);
  not not_5 (not_5_out, W1);
  not not_6 (not_6_out, W0);
endmodule

module OUT (
  input  R2,
  input  R1,
  input  R0,
  input  R_Bus,
  input  W2,
  input  W1,
  input  W0,
  input  Clock,
  output W_Bus
);

  wire and_1_out, and_2_out, controlled_buffer_1_out, not_1_out, not_2_out, not_3_out, not_4_out,
       register_1_q;

  not not_1 (not_1_out, R2);
  and and_1 (and_1_out, not_1_out, not_2_out, R0);
  not not_2 (not_2_out, R1);
  assign controlled_buffer_1_out = and_1_out ? R_Bus : 1'bz;  // Controlled_Buffer controlled_buffer_1
  assign W_Bus = and_2_out ? register_1_q : 1'bz;  // Controlled_Buffer controlled_buffer_2
  and and_2 (and_2_out, not_3_out, not_4_out, W0);
  Register #(.width(1)) register_1 (.D(controlled_buffer_1_out), .Q(register_1_q), .clk(Clock));  // open: en, clr
  not not_3 (not_3_out, W2);
  not not_4 (not_4_out, W1);
endmodule

module IN (
  input  R2,
  input  R1,
  input  R0,
  input  R_Bus,
  input  W2,
  input  W1,
  input  W0,
  input  Clock,
  output W_Bus
);

  wire and_1_out, and_2_out, controlled_buffer_1_out, not_1_out, not_2_out, not_3_out, not_4_out,
       register_1_q;

  not not_1 (not_1_out, R2);
  and and_1 (and_1_out, not_1_out, R1, not_2_out);
  assign controlled_buffer_1_out = and_1_out ? R_Bus : 1'bz;  // Controlled_Buffer controlled_buffer_1
  not not_2 (not_2_out, R0);
  assign W_Bus = and_2_out ? register_1_q : 1'bz;  // Controlled_Buffer controlled_buffer_2
  and and_2 (and_2_out, not_3_out, W1, not_4_out);
  Register #(.width(1)) register_1 (.D(controlled_buffer_1_out), .Q(register_1_q), .clk(Clock));  // open: en, clr
  not not_3 (not_3_out, W2);
  not not_4 (not_4_out, W0);
endmodule

module AC (
  input  R2,
  input  R1,
  input  R0,
  input  R_Bus,
  input  W2,
  input  W1,
  input  W0,
  input  Clock,
  output W_Bus
);

  wire and_1_out, and_2_out, controlled_buffer_1_out, not_1_out, not_2_out, register_1_q;

  not not_1 (not_1_out, R2);
  and and_1 (and_1_out, not_1_out, R1, R0);
  assign controlled_buffer_1_out = and_1_out ? R_Bus : 1'bz;  // Controlled_Buffer controlled_buffer_1
  assign W_Bus = and_2_out ? register_1_q : 1'bz;  // Controlled_Buffer controlled_buffer_2
  and and_2 (and_2_out, not_2_out, W1, W0);
  Register #(.width(1)) register_1 (.D(controlled_buffer_1_out), .Q(register_1_q), .clk(Clock));  // open: en, clr
  not not_2 (not_2_out, W2);
endmodule

module MBR (
  input  R2,
  input  R1,
  input  R0,
  input  R_Bus,
  input  W2,
  input  W1,
  input  W0,
  input  Clock,
  output W_Bus
);

  wire and_1_out, and_2_out, controlled_buffer_1_out, not_1_out, not_2_out, not_3_out, not_4_out,
       register_1_q;

  and and_1 (and_1_out, R2, not_1_out, not_2_out);
  not not_1 (not_1_out, R1);
  assign controlled_buffer_1_out = and_1_out ? R_Bus : 1'bz;  // Controlled_Buffer controlled_buffer_1
  not not_2 (not_2_out, R0);
  assign W_Bus = and_2_out ? register_1_q : 1'bz;  // Controlled_Buffer controlled_buffer_2
  and and_2 (and_2_out, W2, not_3_out, not_4_out);
  Register #(.width(1)) register_1 (.D(controlled_buffer_1_out), .Q(register_1_q), .clk(Clock));  // open: en, clr
  not not_3 (not_3_out, W1);
  not not_4 (not_4_out, W0);
endmodule

module PC (
  input  R2,
  input  R1,
  input  R0,
  input  R_Bus,
  input  W2,
  input  W1,
  input  W0,
  input  Clock,
  output W_Bus
);

  wire and_1_out, and_2_out, controlled_buffer_1_out, not_1_out, not_2_out, register_1_q;

  and and_1 (and_1_out, R2, not_1_out, R0);
  not not_1 (not_1_out, R1);
  assign controlled_buffer_1_out = and_1_out ? R_Bus : 1'bz;  // Controlled_Buffer controlled_buffer_1
  assign W_Bus = and_2_out ? register_1_q : 1'bz;  // Controlled_Buffer controlled_buffer_2
  and and_2 (and_2_out, W2, not_2_out, W0);
  Register #(.width(1)) register_1 (.D(controlled_buffer_1_out), .Q(register_1_q), .clk(Clock));  // open: en, clr
  not not_2 (not_2_out, W1);
endmodule

module MAR (
  input  R2,
  input  R1,
  input  R0,
  input  R_Bus,
  input  W2,
  input  W1,
  input  W0,
  input  Clock,
  output W_Bus
);

  wire and_1_out, and_2_out, controlled_buffer_1_out, not_1_out, not_2_out, register_1_q;

  and and_1 (and_1_out, R2, R1, not_1_out);
  not not_1 (not_1_out, R0);
  assign controlled_buffer_1_out = and_1_out ? R_Bus : 1'bz;  // Controlled_Buffer controlled_buffer_1
  assign W_Bus = and_2_out ? register_1_q : 1'bz;  // Controlled_Buffer controlled_buffer_2
  and and_2 (and_2_out, W2, W1, not_2_out);
  Register #(.width(1)) register_1 (.D(controlled_buffer_1_out), .Q(register_1_q), .clk(Clock));  // open: en, clr
  not not_2 (not_2_out, W0);
endmodule

module Main_Memory (
  input  R0,
  input  R_Bus,
  input  R1,
  input  R2,
  input  W0,
  input  W1,
  input  W2,
  input  Clock,
  output W_Bus
);

  wire and_1_out, and_2_out, controlled_buffer_2_out, register_1_q;

  assign W_Bus = and_2_out ? register_1_q : 1'bz;  // Controlled_Buffer controlled_buffer_1
  and and_1 (and_1_out, R0, R1, R2);
  assign controlled_buffer_2_out = and_1_out ? R_Bus : 1'bz;  // Controlled_Buffer controlled_buffer_2
  Register #(.width(1)) register_1 (.D(controlled_buffer_2_out), .Q(register_1_q), .clk(Clock));  // open: en, clr
  and and_2 (and_2_out, W0, W1, W2);
endmodule
