// Logisim project part_1.circ as structural Verilog: 3 circuits, main circuit main
module main (
  input  [2:0] Write_Control,
  input  [2:0] Read_Control,
  output [15:0] Data_Bus,
  output [15:0] out_4
);

  wire busif_1_read_enable, busif_2_read_enable, busif_3_read_enable, clock_1_out;
  wire [15:0] busif_1_if_to_reg, busif_2_if_to_reg, busif_3_if_to_reg, register_1_q, register_2_q,
       register_3_q;

  Clock clock_1 (.out(clock_1_out));
  busif busif_1 (
    .Bus_to_IF(Data_Bus), .IF_to_Bus(Data_Bus), .Bus_ID(3'b000), .Bus_Write(Write_Control),
    .Bus_Read(Read_Control), .IF_to_Reg(busif_1_if_to_reg), .Reg_to_IF(register_1_q),
    .Read_Enable(busif_1_read_enable));
  busif busif_2 (
    .Bus_to_IF(Data_Bus), .IF_to_Bus(Data_Bus), .Bus_ID(3'b001), .Bus_Write(Write_Control),
    .Bus_Read(Read_Control), .IF_to_Reg(busif_2_if_to_reg), .Reg_to_IF(register_2_q),
    .Read_Enable(busif_2_read_enable));
  Register #(.width(16)) register_1 (
    .D(busif_1_if_to_reg), .en(busif_1_read_enable), .Q(register_1_q), .clk(clock_1_out));  // open: clr
  Register #(.width(16)) register_2 (
    .D(busif_2_if_to_reg), .en(busif_2_read_enable), .Q(register_2_q), .clk(clock_1_out));  // open: clr
  busif busif_3 (
    .Bus_to_IF(Data_Bus), .IF_to_Bus(Data_Bus), .Bus_ID(3'b010), .Bus_Write(Write_Control),
    .Bus_Read(Read_Control), .IF_to_Reg(busif_3_if_to_reg), .Reg_to_IF(register_3_q),
    .Read_Enable(busif_3_read_enable));
  Register #(.width(16)) register_3 (
    .D(busif_3_if_to_reg), .en(busif_3_read_enable), .Q(register_3_q), .clk(clock_1_out));  // open: clr
  alu ALU (.A(register_1_q), .B(register_2_q), .Function(2'b00), .Result(out_4));

  // Notes on the sheet:
  //   MARIE Architecture Part 1
  //   Mike Little, Mark Vaughn, Trevin Teacutter, Caleb Tucker
endmodule

module busif (
  input  [2:0] Bus_Read,
  input  [2:0] Bus_Write,
  input  [15:0] Bus_to_IF,
  input  [2:0] Bus_ID,
  input  [15:0] Reg_to_IF,
  output [15:0] IF_to_Bus,
  output [15:0] IF_to_Reg,
  output Read_Enable
);

  wire comparator_2_eq;

  Comparator #(.width(3)) comparator_1 (.a(Bus_ID), .b(Bus_Read), .eq(Read_Enable));  // open: gt, lt
  assign IF_to_Reg = Read_Enable ? Bus_to_IF : 16'bz;  // Controlled_Buffer controlled_buffer_1
  Comparator #(.width(3)) comparator_2 (.a(Bus_ID), .b(Bus_Write), .eq(comparator_2_eq));  // open: gt, lt
  assign IF_to_Bus = comparator_2_eq ? Reg_to_IF : 16'bz;  // Controlled_Buffer controlled_buffer_2
endmodule

module alu (
  input  [15:0] A,
  input  [1:0] Function,
  input  [15:0] B,
  output [15:0] Result
);

  wire [15:0] adder_1_out, subtractor_1_out;

  Adder #(.width(16)) adder_1 (.a(A), .b(B), .out(adder_1_out));  // open: cin, cout
  Subtractor #(.width(16)) subtractor_1 (.a(A), .b(B), .out(subtractor_1_out));  // open: bin, bout
  Multiplexer #(.select(2), .width(16), .enable("false")) multiplexer_1 (
    .in0(A), .in1(adder_1_out), .in2(subtractor_1_out), .in3({16{1'b0}}), .out(Result), .sel(Function));
endmodule
