// Logisim project part_2.circ as structural Verilog: 8 circuits, main circuit main
module main (
  input  [2:0] Write_Control,
  input  [2:0] Read_Control,
  input  [1:0] Function,
  output [15:0] Data_Bus
);

  wire busif_1_read_enable, busif_2_read_enable, busif_3_read_enable, busif_4_read_enable,
       busif_5_read_enable, busif_6_read_enable, busif_7_read_enable, busif_8_read_enable, clock_1_out;
  wire [11:0] mar_1_memory_input;
  wire [15:0] ac_1_bus_output, alu_1_result, busif_1_if_to_reg, busif_2_if_to_reg, busif_3_if_to_reg,
       busif_4_if_to_reg, busif_5_if_to_reg, busif_6_if_to_reg, busif_7_if_to_reg, busif_8_if_to_reg, IN_q,
       ir_1_bus_output, mar_1_bus_output, MBR_q, mem_1_bus_output, OUT_q, pc_1_bus_output;

  Clock clock_1 (.out(clock_1_out));
  busif busif_1 (
    .Bus_Read(Read_Control), .Bus_Write(Write_Control), .Bus_to_IF(Data_Bus), .IF_to_Bus(Data_Bus),
    .Bus_ID(3'b111), .IF_to_Reg(busif_1_if_to_reg), .Reg_to_IF(ir_1_bus_output),
    .Read_Enable(busif_1_read_enable));
  busif busif_2 (
    .Bus_Read(Read_Control), .Bus_Write(Write_Control), .Bus_to_IF(Data_Bus), .IF_to_Bus(Data_Bus),
    .Bus_ID(3'b110), .IF_to_Reg(busif_2_if_to_reg), .Reg_to_IF(OUT_q), .Read_Enable(busif_2_read_enable));
  ir ir_1 (
    .Bus_Input(busif_1_if_to_reg), .Enable(busif_1_read_enable), .Bus_Output(ir_1_bus_output),
    .Clock(clock_1_out));
  Register #(.width(16)) OUT (
    .D(busif_2_if_to_reg), .en(busif_2_read_enable), .Q(OUT_q), .clk(clock_1_out));  // open: clr
  busif busif_3 (
    .Bus_Read(Read_Control), .Bus_Write(Write_Control), .Bus_to_IF(Data_Bus), .IF_to_Bus(Data_Bus),
    .Bus_ID(3'b101), .IF_to_Reg(busif_3_if_to_reg), .Reg_to_IF(IN_q), .Read_Enable(busif_3_read_enable));
  Register #(.width(16)) IN (
    .D(busif_3_if_to_reg), .en(busif_3_read_enable), .Q(IN_q), .clk(clock_1_out));  // open: clr
  busif busif_4 (
    .Bus_Read(Read_Control), .Bus_Write(Write_Control), .Bus_to_IF(Data_Bus), .IF_to_Bus(Data_Bus),
    .Bus_ID(3'b100), .IF_to_Reg(busif_4_if_to_reg), .Reg_to_IF(ac_1_bus_output),
    .Read_Enable(busif_4_read_enable));
  busif busif_5 (
    .Bus_Read(Read_Control), .Bus_Write(Write_Control), .Bus_to_IF(Data_Bus), .IF_to_Bus(Data_Bus),
    .Bus_ID(3'b011), .IF_to_Reg(busif_5_if_to_reg), .Reg_to_IF(MBR_q), .Read_Enable(busif_5_read_enable));
  ac ac_1 (
    .Bus_Input(busif_4_if_to_reg), .Enable(busif_4_read_enable), .Bus_Output(ac_1_bus_output),
    .Function(Function), .Clock(clock_1_out), .ALU_Input(alu_1_result));
  Register #(.width(16)) MBR (
    .D(busif_5_if_to_reg), .en(busif_5_read_enable), .Q(MBR_q), .clk(clock_1_out));  // open: clr
  alu alu_1 (.A(ac_1_bus_output), .B(MBR_q), .Function(Function), .Result(alu_1_result));
  busif busif_6 (
    .Bus_Read(Read_Control), .Bus_Write(Write_Control), .Bus_to_IF(Data_Bus), .IF_to_Bus(Data_Bus),
    .Bus_ID(3'b010), .IF_to_Reg(busif_6_if_to_reg), .Reg_to_IF(pc_1_bus_output),
    .Read_Enable(busif_6_read_enable));
  pc pc_1 (
    .Enable(busif_6_read_enable), .Bus_Input(busif_6_if_to_reg), .Bus_Output(pc_1_bus_output),
    .Clock(clock_1_out));
  busif busif_7 (
    .Bus_Read(Read_Control), .Bus_Write(Write_Control), .Bus_to_IF(Data_Bus), .IF_to_Bus(Data_Bus),
    .Bus_ID(3'b001), .IF_to_Reg(busif_7_if_to_reg), .Reg_to_IF(mar_1_bus_output),
    .Read_Enable(busif_7_read_enable));
  mar mar_1 (
    .Bus_Input(busif_7_if_to_reg), .Enable(busif_7_read_enable), .Bus_Output(mar_1_bus_output),
    .Memory_Input(mar_1_memory_input), .Clock(clock_1_out));
  busif busif_8 (
    .Bus_Read(Read_Control), .Bus_Write(Write_Control), .Bus_to_IF(Data_Bus), .IF_to_Bus(Data_Bus),
    .Bus_ID(3'b000), .IF_to_Reg(busif_8_if_to_reg), .Reg_to_IF(mem_1_bus_output),
    .Read_Enable(busif_8_read_enable));
  mem mem_1 (
    .Memory_Address(mar_1_memory_input), .Bus_Input(busif_8_if_to_reg), .Enable(busif_8_read_enable),
    .Clock(clock_1_out), .Bus_Output(mem_1_bus_output));

  // Notes on the sheet:
  //   MARIE Architecture Part 2
  //   Mike Little, Mark Vaughn, Trevin Teacutter, Caleb Tucker
endmodule

module busif (
  input  [2:0] Bus_Read,
  input  [2:0] Bus_Write,
  input  [15:0] Bus_to_IF,
  input  [2:0] Bus_ID,
  input  [15:0] Reg_to_IF,
  output [15:0] IF_to_Bus,
  output [15:0] IF_to_Reg,
  output Read_Enable
);

  wire comparator_2_eq;

  Comparator #(.width(3)) comparator_1 (.a(Bus_ID), .b(Bus_Read), .eq(Read_Enable));  // open: gt, lt
  assign IF_to_Reg = Read_Enable ? Bus_to_IF : 16'bz;  // Controlled_Buffer controlled_buffer_1
  Comparator #(.width(3)) comparator_2 (.a(Bus_ID), .b(Bus_Write), .eq(comparator_2_eq));  // open: gt, lt
  assign IF_to_Bus = comparator_2_eq ? Reg_to_IF : 16'bz;  // Controlled_Buffer controlled_buffer_2
endmodule

// ALU
module alu (
  input  [1:0] Function,
  input  [15:0] B,
  input  [15:0] A,
  output [15:0] Result
);

  wire [15:0] adder_1_out, subtractor_1_out;

  Adder #(.width(16)) adder_1 (.a(A), .b(B), .out(adder_1_out));  // open: cin, cout
  Subtractor #(.width(16)) subtractor_1 (.a(A), .b(B), .out(subtractor_1_out));  // open: bin, bout
  Multiplexer #(.select(2), .width(16), .enable("false")) multiplexer_1 (
    .in0(A), .in1(adder_1_out), .in2(subtractor_1_out), .in3({16{1'b0}}), .out(Result), .sel(Function));
endmodule

// PC
module pc (
  input  [15:0] Bus_Input,
  input  Clock,
  input  Enable,
  output [15:0] Bus_Output
);

  wire [15:0] register_1_q;

  Register #(.width(16)) register_1 (.D(Bus_Input), .en(Enable), .Q(register_1_q), .clk(Clock));  // open: clr
  Adder #(.width(16)) adder_1 (.a(register_1_q), .b(16'h1), .out(Bus_Output));  // open: cin, cout
endmodule

// IR
module ir (
  input  [15:0] Bus_Input,
  input  Clock,
  input  Enable,
  output [15:0] Bus_Output
);

  wire [15:0] register_1_q;

  Register #(.width(16)) register_1 (.D(Bus_Input), .en(Enable), .Q(register_1_q), .clk(Clock));  // open: clr
  assign Bus_Output = {{4{1'b0}}, register_1_q[11:0]};  // Bit_Extender bit_extender_1
endmodule

// AC
module ac (
  input  [15:0] Bus_Input,
  input  Enable,
  input  [1:0] Function,
  input  Clock,
  input  [15:0] ALU_Input,
  output [15:0] Bus_Output
);

  wire or_1_out, or_2_out;
  wire [15:0] multiplexer_1_out;

  Multiplexer #(.select(2), .width(16), .enable("false")) multiplexer_1 (
    .in0(Bus_Input), .in1(ALU_Input), .in2(ALU_Input), .in3(ALU_Input), .out(multiplexer_1_out),
    .sel(Function));
  or or_1 (or_1_out, Enable, or_2_out);
  or or_2 (or_2_out, Function[1], Function[0]);
  Register #(.width(16)) register_1 (.D(multiplexer_1_out), .en(or_1_out), .Q(Bus_Output), .clk(Clock));  // open: clr
endmodule

// MEM
module mem (
  input  [11:0] Memory_Address,
  input  [15:0] Bus_Input,
  input  Enable,
  input  Clock,
  output [15:0] Bus_Output
);

  RAM #(.addrWidth(12), .dataWidth(16), .bus("separate")) ram_1 (
    .addr(Memory_Address), .din(Bus_Input), .data(Bus_Output), .str(Enable), .clk(Clock));  // open: sel, ld, clr
endmodule

// MAR
module mar (
  input  [15:0] Bus_Input,
  input  Clock,
  input  Enable,
  output [15:0] Bus_Output,
  output [11:0] Memory_Input
);

  Register #(.width(16)) register_1 (.D(Bus_Input), .en(Enable), .Q(Bus_Output), .clk(Clock));  // open: clr

  assign Memory_Input = Bus_Output[11:0];
endmodule
