// Logisim project project_test.circ as structural Verilog: 1 circuit, main circuit main
module main (
);

  Adder adder_1 ();  // open: a, b, out, cin, cout
  Counter #(.width(16), .max('hffff)) ACC ();  // open: load, D, count, Q, carry, clk, clr
  Register #(.width(16)) IR ();  // open: D, en, Q, clk, clr
  Register #(.width(12)) PC ();  // open: D, en, Q, clk, clr
  Register #(.width(12)) MAR ();  // open: D, en, Q, clk, clr
  Subtractor subtractor_1 ();  // open: a, b, out, bin, bout
  Register INPUT ();  // open: D, en, Q, clk, clr
  Register OUTPUT ();  // open: D, en, Q, clk, clr
  ROM #(.addrWidth(12), .dataWidth(4)) rom_1 ();  // open: addr, data, sel

  // Notes on the sheet:
  //   Memory
  //   contents of rom_1 (hex, n*v repeats v):
  //   4*f 4*a 4*b 4*1 4*2 4*3 4*4
endmodule
